// Digital circuit counter_4b.dig as structural Verilog
module counter_4b (
  input  clk,
  output Q_0,
  output Q_1,
  output Q_2,
  output Q_3
);

  D_FF d_ff_1 ();  // open: D, C, Q, nQ
endmodule

/* Test case:
           clk Q_3 Q_2 Q_1 Q_0
repeat(16)  C  bits(4,n+1)
*/
